// Logisim project Final_4Bit_CPU.circ as structural Verilog: 12 circuits, main circuit CPU
module ALU (
  input  [3:0] A,
  input  [3:0] B,
  input  [1:0] AFS,
  input  SUB,
  output [3:0] ALU_OUT
);

  wire [3:0] add_4bit_1_add4, and_4bit_1_and4, not_1_out, or_4bit_1_or4, Sub_Enable_f, xor_4bit_1_xor4;

  assign not_1_out = ~B;  // NOT_Gate not_1, 4 bits wide
  MUX2to1_4bit Sub_Enable (.A(B), .B(not_1_out), .S(SUB), .F(Sub_Enable_f));
  XOR_4bit xor_4bit_1 (.A(A), .B(B), .XOR4(xor_4bit_1_xor4));
  AND_4bit and_4bit_1 (.A(A), .B(B), .AND4(and_4bit_1_and4));
  OR_4bit or_4bit_1 (.A(A), .B(B), .OR4(or_4bit_1_or4));
  Add_4bit add_4bit_1 (.A(A), .SUB_In(SUB), .B(Sub_Enable_f), .ADD4(add_4bit_1_add4));
  MUX4to1_4bit mux4to1_4bit_1 (
    .IN0(xor_4bit_1_xor4), .IN2(or_4bit_1_or4), .IN1(and_4bit_1_and4), .IN3(add_4bit_1_add4), .RSS(AFS),
    .MUX_out(ALU_OUT));

  // Notes on the sheet:
  //   Adam J Sandland
endmodule

module MUX2to1_1bit (
  input  A,
  input  S,
  input  B,
  output F
);

  wire and_1_out, and_2_out, not_1_out;

  not not_1 (not_1_out, S);
  and and_1 (and_1_out, A, not_1_out);
  and and_2 (and_2_out, S, B);
  or or_1 (F, and_1_out, and_2_out);
endmodule

module MUX2to1_4bit (
  input  [3:0] A,
  input  [3:0] B,
  input  S,
  output [3:0] F
);

  MUX2to1_1bit mux2to1_1bit_1 (.A(A[3]), .S(S), .B(B[3]), .F(F[3]));
  MUX2to1_1bit mux2to1_1bit_2 (.A(A[2]), .S(S), .B(B[2]), .F(F[2]));
  MUX2to1_1bit mux2to1_1bit_3 (.A(A[1]), .S(S), .B(B[1]), .F(F[1]));
  MUX2to1_1bit mux2to1_1bit_4 (.A(A[0]), .S(S), .B(B[0]), .F(F[0]));
endmodule

module Full_Adder (
  input  A,
  input  B,
  input  Cin,
  output S,
  output Cout
);

  wire and_1_out, and_2_out, and_3_out;

  and and_1 (and_1_out, A, B);
  and and_2 (and_2_out, B, Cin);
  and and_3 (and_3_out, A, Cin);
  xor xor_1 (S, A, B, Cin);
  or or_1 (Cout, and_1_out, and_2_out, and_3_out);
endmodule

module AND_4bit (
  input  [3:0] A,
  input  [3:0] B,
  output [3:0] AND4
);

  and and_1 (AND4[3], A[3], B[3]);
  and and_2 (AND4[2], A[2], B[2]);
  and and_3 (AND4[1], A[1], B[1]);
  and and_4 (AND4[0], A[0], B[0]);
endmodule

module OR_4bit (
  input  [3:0] A,
  input  [3:0] B,
  output [3:0] OR4
);

  or or_1 (OR4[3], A[3], B[3]);
  or or_2 (OR4[2], A[2], B[2]);
  or or_3 (OR4[1], A[1], B[1]);
  or or_4 (OR4[0], A[0], B[0]);
endmodule

module XOR_4bit (
  input  [3:0] A,
  input  [3:0] B,
  output [3:0] XOR4
);

  xor xor_1 (XOR4[3], A[3], B[3]);
  xor xor_2 (XOR4[2], A[2], B[2]);
  xor xor_3 (XOR4[1], A[1], B[1]);
  xor xor_4 (XOR4[0], A[0], B[0]);
endmodule

module MUX4to1_4bit (
  input  [3:0] IN0,
  input  [3:0] IN2,
  input  [3:0] IN1,
  input  [3:0] IN3,
  input  [1:0] RSS,
  output [3:0] MUX_out
);

  wire [3:0] mux2to1_4bit_1_f, mux2to1_4bit_2_f;

  MUX2to1_4bit mux2to1_4bit_1 (.A(IN0), .B(IN2), .S(RSS[1]), .F(mux2to1_4bit_1_f));
  MUX2to1_4bit mux2to1_4bit_2 (.A(IN1), .B(IN3), .S(RSS[1]), .F(mux2to1_4bit_2_f));
  MUX2to1_4bit mux2to1_4bit_3 (.A(mux2to1_4bit_1_f), .B(mux2to1_4bit_2_f), .S(RSS[0]), .F(MUX_out));

  // Notes on the sheet:
  //   (A input)
  //   (C input)
  //   (B input)
  //   (D input)
  //   Adam J Sandland
  //   (F)
endmodule

module Add_4bit (
  input  [3:0] A,
  input  SUB_In,
  input  [3:0] B,
  output [3:0] ADD4
);

  wire full_adder_1_cout, full_adder_2_cout, full_adder_3_cout, full_adder_4_cout;

  Full_Adder full_adder_1 (.A(A[0]), .B(B[0]), .Cin(SUB_In), .S(ADD4[0]), .Cout(full_adder_1_cout));
  Full_Adder full_adder_2 (.A(A[1]), .B(B[1]), .Cin(full_adder_1_cout), .S(ADD4[1]), .Cout(full_adder_2_cout));
  Full_Adder full_adder_3 (.A(A[2]), .B(B[2]), .Cin(full_adder_2_cout), .S(ADD4[2]), .Cout(full_adder_3_cout));
  Full_Adder full_adder_4 (.A(A[3]), .B(B[3]), .Cin(full_adder_3_cout), .S(ADD4[3]), .Cout(full_adder_4_cout));
  // also tied to GND on the sheet: full_adder_4_cout

  // Notes on the sheet:
  //   Adam J Sandland
endmodule

module CPU (
  input  reset
);

  wire DWE, SUB, undriven, undriven_2, WCLK, WE;
  wire [1:0] AFS, RSS;
  wire [2:0] AddrA, AddrB, AddrD;
  wire [3:0] ALU_Out, mux4to1_4bit_1_mux_out, PortA, PortB;
  wire [7:0] counter_1_q;
  wire [15:3] rom_1_data;

  Counter counter_1 (
    .clr(reset), .load(undriven), .up(undriven_2), .count(undriven_2), .clk(WCLK), .Q(counter_1_q));  // open: D, carry
  Clock CLK (.out(WCLK));
  ROM #(.dataWidth(16)) rom_1 (
    .addr(counter_1_q), .data({rom_1_data[15:11], AddrD, rom_1_data[7], AddrA, rom_1_data[3], AddrB}));
  ROM #(.addrWidth(4), .dataWidth(7)) rom_2 (.addr(rom_1_data[15:12]), .data({SUB, AFS, RSS, DWE, WE}));
  MUX4to1_4bit mux4to1_4bit_1 (
    .IN0({rom_1_data[3], AddrB}), .IN2(PortA), .IN1(ALU_Out), .RSS(RSS), .MUX_out(mux4to1_4bit_1_mux_out));  // open: IN3
  Register_File register_file_1 (
    .RAddrA(AddrA), .RAddrB(AddrB), .WE(WE), .WAddr(AddrD), .Data_in(mux4to1_4bit_1_mux_out), .Clk(WCLK),
    .PortA(PortA), .PortB(PortB));
  TTY tty_1 (.data({PortA[2:0], PortB}), .clk(WCLK), .we(DWE));  // open: clr
  ALU alu_1 (.A(PortA), .B(PortB), .AFS(AFS), .SUB(SUB), .ALU_OUT(ALU_Out));

  // Notes on the sheet:
  //   contents of rom_1 (hex, n*v repeats v):
  //   1003 1104 1203 1302 1402 150b 1603 170d 3001 3045 3023 3067 7513 3005
  //   contents of rom_2 (hex, n*v repeats v):
  //   0 1 9 2 5 15 25 35 7*0 75
  //   Adam Sandland
endmodule

module Register_File (
  input  [2:0] RAddrA,
  input  [2:0] RAddrB,
  input  WE,
  input  [2:0] WAddr,
  input  [3:0] Data_in,
  input  Clk,
  output [3:0] PortA,
  output [3:0] PortB
);

  wire decoder_1_out0, decoder_1_out1, decoder_1_out2, decoder_1_out3, decoder_1_out4, decoder_1_out5,
       decoder_1_out6, decoder_1_out7;
  wire [3:0] D0, D1, D2, D3, D4, D5, D6, D7;

  Decoder #(.select(3)) decoder_1 (
    .out0(decoder_1_out0), .out1(decoder_1_out1), .out2(decoder_1_out2), .out3(decoder_1_out3),
    .out4(decoder_1_out4), .out5(decoder_1_out5), .out6(decoder_1_out6), .out7(decoder_1_out7), .sel(WAddr),
    .en(WE));
  Four_bit_register four_bit_register_1 (.Din(Data_in), .Write_EN(decoder_1_out0), .Clk(Clk), .Dout(D0));
  Four_bit_register four_bit_register_2 (.Din(Data_in), .Write_EN(decoder_1_out1), .Clk(Clk), .Dout(D1));
  Four_bit_register four_bit_register_3 (.Din(Data_in), .Write_EN(decoder_1_out2), .Clk(Clk), .Dout(D2));
  Four_bit_register four_bit_register_4 (.Din(Data_in), .Write_EN(decoder_1_out3), .Clk(Clk), .Dout(D3));
  Four_bit_register four_bit_register_5 (.Din(Data_in), .Write_EN(decoder_1_out4), .Clk(Clk), .Dout(D4));
  Four_bit_register four_bit_register_6 (.Din(Data_in), .Write_EN(decoder_1_out5), .Clk(Clk), .Dout(D5));
  Four_bit_register four_bit_register_7 (.Din(Data_in), .Write_EN(decoder_1_out6), .Clk(Clk), .Dout(D6));
  Four_bit_register four_bit_register_8 (.Din(Data_in), .Write_EN(decoder_1_out7), .Clk(Clk), .Dout(D7));
  Multiplexer #(.select(3), .width(4)) multiplexer_1 (
    .in0(D0), .in1(D1), .in2(D2), .in3(D3), .in4(D4), .in5(D5), .in6(D6), .in7(D7), .out(PortA), .sel(RAddrA));
  Multiplexer #(.select(3), .width(4)) multiplexer_2 (
    .in0(D0), .in1(D1), .in2(D2), .in3(D3), .in4(D4), .in5(D5), .in6(D6), .in7(D7), .out(PortB), .sel(RAddrB));
endmodule

module Four_bit_register (
  input  [3:0] Din,
  input  Write_EN,
  input  Clk,
  output [3:0] Dout
);

  wire multiplexer_1_out, multiplexer_2_out, multiplexer_3_out, multiplexer_4_out;

  D_Flip_Flop d_ff_1 (.D(multiplexer_1_out), .clk(Clk), .Q(Dout[0]));  // open: Qn, preset, reset
  Multiplexer multiplexer_1 (.in0(Dout[0]), .in1(Din[0]), .out(multiplexer_1_out), .sel(Write_EN));
  D_Flip_Flop d_ff_2 (.D(multiplexer_2_out), .clk(Clk), .Q(Dout[1]));  // open: Qn, preset, reset
  Multiplexer multiplexer_2 (.in0(Dout[1]), .in1(Din[1]), .out(multiplexer_2_out), .sel(Write_EN));
  D_Flip_Flop d_ff_3 (.D(multiplexer_3_out), .clk(Clk), .Q(Dout[2]));  // open: Qn, preset, reset
  Multiplexer multiplexer_3 (.in0(Dout[2]), .in1(Din[2]), .out(multiplexer_3_out), .sel(Write_EN));
  D_Flip_Flop d_ff_4 (.D(multiplexer_4_out), .clk(Clk), .Q(Dout[3]));  // open: Qn, preset, reset
  Multiplexer multiplexer_4 (.in0(Dout[3]), .in1(Din[3]), .out(multiplexer_4_out), .sel(Write_EN));
endmodule
